# Fritzing sketch TecladoNFP-Ligação dos fios (saved by Fritzing 1.0.1rc)

parts:
  Arduino_32u4 = Arduino Micro (Rev3)
  HC-05/HC-06 = Bluetooth HC-05 Macho

nets:
  GND: Arduino_32u4.GND, HC-05/HC-06.GND
  N1: Arduino_32u4.D8_PWM/A8, HC-05/HC-06.TXD
  N2: Arduino_32u4.D9_PWM/A9, HC-05/HC-06.RXD
  5V: Arduino_32u4.5V, HC-05/HC-06.VCC
